# Fritzing sketch rfid_reader (saved by Fritzing 0.9.5d)
perfboards: 2

parts:
  Raspberry_Pi_1 = Raspberry Pi 3 [part_number=RPI-3-V1.2]
  Part1 = RFID-RC522-v2
  J18 = female pin header, 2 pins [form="♀ (female)"]  # not connected
  J14 = female pin header, 2 pins [form="♀ (female)"]
  J2 = female pin header, 2 pins [form="♀ (female)"]
  J9 = female pin header, 2 pins [form="♀ (female)"]
  J4 = female pin header, 2 pins [form="♀ (female)"]
  J8 = female pin header, 2 pins [form="♀ (female)"]
  J10 = female pin header, 2 pins [form="♀ (female)"]  # not connected
  J16 = female pin header, 2 pins [form="♀ (female)"]  # not connected
  J20 = female pin header, 2 pins [form="♀ (female)"]  # not connected
  J19 = female pin header, 2 pins [form="♀ (female)"]  # not connected
  J6 = female pin header, 2 pins [form="♀ (female)"]
  J1 = female pin header, 2 pins [form="♀ (female)"]
  J15 = female pin header, 2 pins [form="♀ (female)"]  # not connected
  J12 = female pin header, 2 pins [form="♀ (female)"]
  J17 = female pin header, 2 pins [form="♀ (female)"]  # not connected
  J11 = female pin header, 2 pins [form="♀ (female)"]
  J5 = female pin header, 2 pins [form="♀ (female)"]
  J7 = female pin header, 2 pins [form="♀ (female)"]
  J13 = female pin header, 2 pins [form="♀ (female)"]
  J3 = female pin header, 2 pins [form="♀ (female)"]
  J21 = female pin header, 2 pins [form="♀ (female)"]  # not connected
  J22 = female pin header, 2 pins [form="♀ (female)"]  # not connected
  J23 = female pin header, 2 pins [form="♀ (female)"]  # not connected
  J24 = female pin header, 2 pins [form="♀ (female)"]  # not connected
  J25 = female pin header, 2 pins [form="♀ (female)"]  # not connected
  J26 = female pin header, 2 pins [form="♀ (female)"]
  J28 = female pin header, 2 pins [form="♀ (female)"]
  J29 = female pin header, 2 pins [form="♀ (female)"]
  J30 = female pin header, 2 pins [form="♀ (female)"]
  J31 = female pin header, 2 pins [form="♀ (female)"]  # not connected
  J32 = female pin header, 2 pins [form="♀ (female)"]
  J33 = female pin header, 2 pins [form="♀ (female)"]
  Mod1 = Passive Buzzer
  Part2 = Adafruit PCF8523 RTC [part_number="Adafruit #3295"]
  LED1 = LED - 3mm [color="Green (555nm)" package="3 mm [THT]"]
  LED2 = LED - 3mm [color="Red (633nm)" package="3 mm [THT]"]
  R1 = Resistor [tolerance=±5% resistance=1k package="1206 [SMD]"]
  R2 = Resistor [tolerance=±5% resistance=220 package="1206 [SMD]"]

nets:
  3V3: Raspberry_Pi_1.3v3, Raspberry_Pi_1.GPIO2, Raspberry_Pi_1.GPIO3, Raspberry_Pi_1.GIPO4, Raspberry_Pi_1.5V, J28.pin1, J28.pin2, J29.pin1, J29.pin2
  N1: Raspberry_Pi_1.GND, Raspberry_Pi_1.GIPO10, Raspberry_Pi_1.ID_SC, Raspberry_Pi_1.GIPO7, Raspberry_Pi_1.GIPO8, J26.pin2, J30.pin1, J30.pin2, J32.pin2
  N2: Raspberry_Pi_1.GIPO9, J33.pin1
  N3: Raspberry_Pi_1.GIPO11, J33.pin2
  N4: Raspberry_Pi_1.GIPO25, J26.pin1
  N5: Part1.SDA, J14.pin1, J12.pin2
  N6: Part1.SCK, J8.pin2, J13.pin1
  N7: Part1.MOSI, Part1.MISO, Part1.RST, J8.pin1, J12.pin1, J11.pin2, J7.pin2
  GND: Part1.IRQ, Part1.GND, J9.pin1, J5.pin1, Mod1.-, Part2.GND, LED1.cathode, LED2.cathode
  3.3V: Part1.3.3V, J2.pin1, J2.pin2, J1.pin1, J1.pin2, Mod1.NC, Part2.SDA, Part2.VCC
  N8: J4.pin1, J3.pin1, Part2.SCL
  N9: J4.pin2, J3.pin2, Mod1.S
  N10: J6.pin1, R2.Pin_0
  N11: J5.pin2, R1.Pin_0
  N12: LED1.anode, R1.Pin_1
  N13: LED2.anode, R2.Pin_1

custom parts:
  RFID-RC522-v2: A simple China made RFID-RC522 Reader; do check the pin labels, as this is a MFRC522 based clone.
  Adafruit PCF8523 RTC: This is a great battery-backed real time clock (RTC) that allows your microcontroller project to keep track of time even if it is reprogrammed, or if the power is lost. Perfect for datalogging, clock-building, time stamping, timers and alarms, etc. Equipped with PCF8523 RTC - it can run from 3.3V or 5V power & logic! Works great with an Arduino using our RTC library, with CircuitPython or with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
