# Fritzing sketch rfid_reader_pi_zero (saved by Fritzing 0.9.3b)
circuit board: 9.51208cm x 7.15801cm
breadboards: 1

parts:
  RASPI_ZERO = Raspberry Pi Zero
  GREEN = LED - 3mm [color="Green (555nm)" current=0.030 package="3 mm [THT]"]
  RED = LED - 3mm [color="Red (633nm)" current=0.030 package="3 mm [THT]"]
  RTC = Adafruit PCF8523 RTC [part_number="Adafruit #3295"]
  RFID = RFID-RC522-v3
  Mod1 = KY-012 Active Buzzer Module [package="Breakout board"]
  R2 = Resistor [tolerance=±5% resistance=220 package=THT]
  R1 = Resistor [tolerance=±5% resistance=1k package=THT]

nets:
  VCC: RASPI_ZERO.pin_1, RASPI_ZERO.pin_17, RTC.VCC, RFID.3.3V, Mod1.NC
  N1: RASPI_ZERO.pin_3, RTC.SDA
  N2: RASPI_ZERO.pin_5, RTC.SCL
  GND: RASPI_ZERO.pin_6, RASPI_ZERO.pin_9, RASPI_ZERO.pin_39, GREEN.cathode, RED.cathode, RTC.GND, RFID.GND, Mod1.S
  N3: RASPI_ZERO.pin_7, Mod1.-
  N4: RASPI_ZERO.pin_11, R1.Pin_1
  N5: RASPI_ZERO.pin_13, R2.Pin_1
  N6: RASPI_ZERO.pin_19, RFID.MOSI
  N7: RASPI_ZERO.pin_21, RFID.MISO
  N8: RASPI_ZERO.pin_22, RFID.RST
  N9: RASPI_ZERO.pin_23, RFID.SCK
  N10: RASPI_ZERO.pin_24, RFID.SDA
  N11: GREEN.anode, R1.Pin_0
  N12: RED.anode, R2.Pin_0

notes:
  github.com/d-rk
  rev 1.1

custom parts:
  Adafruit PCF8523 RTC: This is a great battery-backed real time clock (RTC) that allows your microcontroller project to keep track of time even if it is reprogrammed, or if the power is lost. Perfect for datalogging, clock-building, time stamping, timers and alarms, etc. Equipped with PCF8523 RTC - it can run from 3.3V or 5V power & logic! Works great with an Arduino using our RTC library, with CircuitPython or with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
  RFID-RC522-v3: A simple China made RFID-RC522 Reader (6x4 cm); do check the pin labels, as this is a MFRC522 based clone.
  KY-012 Active Buzzer Module: Active Piezoelectric Buzzer Module KY-012, it produces single-tone sound when signal is high. (Special thanks to vanepp for fixing the PCB holes and other errors)
